# Fritzing sketch Automatic-double-doors (saved by Fritzing 0.8.7b)
breadboards: 2

parts:
  Parte1 = Arduino Uno (Rev3)
  Limit-Open-Left = Toggle Switch [package=THT]  # not connected
  Relay-Close-Left = Relay T73
  Relay-Close-Right = Relay T73
  Relay-Open-Right = Relay T73
  Relay-Open-Left = Relay T73
  Limit-Close-Left = Toggle Switch [package=THT]  # not connected
  Limit-Open-Right = Toggle Switch [package=THT]  # not connected
  Limit-Close-Right = Toggle Switch [package=THT]  # not connected
  Relay-Signaling = Relay T73
  Relay-Lock = Relay T73
  Button-Open/Close = Round Pushbutton
  Button-Emergency = Round Pushbutton
  Remote-Open/Close = Round Pushbutton
  Relay-Signaling1 = Relay T73
  J1 = Infrared Proximity Sensor

nets:
  N1: Parte1.D8, Relay-Signaling.C2
  N2: Parte1.D9_PWM, Relay-Lock.C2
  N3: Parte1.D10_PWM/SS, Relay-Close-Right.C2
  N4: Parte1.D11_PWM/MOSI, Relay-Open-Right.C2
  N5: Parte1.D12/MISO, Relay-Close-Left.C2
  N6: Parte1.D13/SCK, Relay-Open-Left.C2
  GND: Parte1.GND, Relay-Close-Right.C1, Relay-Open-Right.C1, Relay-Open-Left.C1, Relay-Signaling.C1, Relay-Lock.C1, Button-Open/Close.leg0, Button-Emergency.leg0, Remote-Open/Close.leg0, Relay-Signaling1.C1, J1.GND
  N7: Parte1.D3_PWM, J1.Vout
  N8: Parte1.D4, Remote-Open/Close.leg1
  N9: Parte1.D5_PWM, Button-Emergency.leg1
  N10: Parte1.D6_PWM, Button-Open/Close.leg1
  N11: Parte1.D7, Relay-Signaling1.C2

custom parts:
  Relay T73: An T73 Mini PCB Relay
